// Logisim project circ.circ as structural Verilog: 2 circuits, main circuit main
module main (
  input  [3:0] in_1,
  output [7:0] out_2
);

  circ circ_1 (
    .e3(in_1[0]), .e2(in_1[1]), .e1(in_1[2]), .e0(in_1[3]), .s7(out_2[0]), .s6(out_2[1]), .s5(out_2[2]),
    .s4(out_2[3]), .s3(out_2[4]), .s2(out_2[5]), .s1(out_2[6]), .s0(out_2[7]));
endmodule

module circ (
  input  e3,
  input  e2,
  input  e1,
  input  e0,
  output s7,
  output s6,
  output s5,
  output s4,
  output s3,
  output s2,
  output s1,
  output s0
);

  wire and_1_out, and_2_out, and_3_out, and_4_out, and_5_out, and_6_out, and_7_out, and_8_out, and_9_out,
       and_10_out, and_11_out, and_12_out, and_13_out, and_14_out, not_1_out, not_2_out, not_3_out,
       not_4_out, not_5_out, not_6_out, not_7_out, not_8_out, not_9_out, not_10_out, not_11_out, not_12_out,
       not_13_out, not_14_out, not_15_out, not_16_out, not_17_out, not_18_out;

  not not_1 (not_1_out, e3);
  and and_1 (and_1_out, not_1_out, e2);
  and and_2 (and_2_out, e3, not_2_out);
  not not_2 (not_2_out, e2);
  not not_3 (not_3_out, e3);
  and and_3 (and_3_out, not_3_out, not_4_out, e1);
  not not_4 (not_4_out, e2);
  not not_5 (not_5_out, e3);
  and and_4 (and_4_out, not_5_out, e2, not_6_out);
  not not_6 (not_6_out, e1);
  and and_5 (and_5_out, e3, not_7_out, not_8_out);
  not not_7 (not_7_out, e2);
  not not_8 (not_8_out, e1);
  and and_6 (and_6_out, e3, e2, e1);
  not not_9 (not_9_out, e3);
  and and_7 (and_7_out, not_9_out, e1);
  and and_8 (and_8_out, e3, not_10_out);
  not not_10 (not_10_out, e1);
  not not_11 (not_11_out, e2);
  and and_9 (and_9_out, not_11_out, not_12_out, e0);
  not not_12 (not_12_out, e1);
  not not_13 (not_13_out, e2);
  and and_10 (and_10_out, not_13_out, e1, not_14_out);
  not not_14 (not_14_out, e0);
  not not_15 (not_15_out, e1);
  and and_11 (and_11_out, e2, not_15_out, not_16_out);
  not not_16 (not_16_out, e0);
  and and_12 (and_12_out, e2, e1, e0);
  not not_17 (not_17_out, e2);
  and and_13 (and_13_out, not_17_out, e0);
  and and_14 (and_14_out, e2, not_18_out);
  not not_18 (not_18_out, e0);
  or or_1 (s5, and_1_out, and_2_out);
  or or_2 (s3, and_3_out, and_4_out, and_5_out, and_6_out);
  or or_3 (s2, and_7_out, and_8_out);
  or or_4 (s1, and_9_out, and_10_out, and_11_out, and_12_out);
  or or_5 (s0, and_13_out, and_14_out);

  assign s4 = e2;
  assign s6 = e3;
  assign s7 = e3;
endmodule
